// Digital circuit CPU.dig as structural Verilog
module CPU (
  input  clk,
  input  CLR_PC
);

  wire _8_to_16_bit_bus_width_converter_1_p4, comparator_1_eq, comparator_2_eq, comparator_3_eq,
       comparator_4_eq, comparator_5_eq, comparator_6_eq, comparator_7_eq, comparator_8_eq, or_1_out,
       or_2_out, or_3_out;
  wire [7:0] alu_1_p1, programme_counter_1_p1;
  wire [15:0] and_1_out, programme_counter_1_p2, programme_counter_1_p7;

  Comparator #(.Bits(8)) comparator_1 (.a(alu_1_p1), .b(8'h1), .eq(comparator_1_eq));  // open: gt, lt
  Comparator #(.Bits(8)) comparator_2 (.a(alu_1_p1), .b(8'h1), .eq(comparator_2_eq));  // open: gt, lt
  Comparator #(.Bits(8)) comparator_3 (.a(alu_1_p1), .b(8'h1), .eq(comparator_3_eq));  // open: gt, lt
  Comparator #(.Bits(8)) comparator_4 (.a(alu_1_p1), .b(8'h1), .eq(comparator_4_eq));  // open: gt, lt
  Comparator #(.Bits(8)) comparator_5 (.a(alu_1_p1), .b(8'h1), .eq(comparator_5_eq));  // open: gt, lt
  Comparator #(.Bits(8)) comparator_6 (.a(alu_1_p1), .b(8'h1), .eq(comparator_6_eq));  // open: gt, lt
  Comparator #(.Bits(8)) comparator_7 (.a(alu_1_p1), .b(8'h1), .eq(comparator_7_eq));  // open: gt, lt
  Comparator #(.Bits(8)) comparator_8 (.a(alu_1_p1), .b(8'h1), .eq(comparator_8_eq));  // open: gt, lt
  // Programme_Counter programme_counter_1: pin names not known; wires that end beside it: programme_counter_1_p1, programme_counter_1_p2, clk, comparator_1_eq, comparator_2_eq, CLR_PC, programme_counter_1_p7
  // ALU alu_1: pin names not known; wires that end beside it: alu_1_p1, programme_counter_1_p1, clk, programme_counter_1_p1
  // _8_to_16_bit_bus_width_converter _8_to_16_bit_bus_width_converter_1: pin names not known; wires that end beside it: programme_counter_1_p1, comparator_3_eq, comparator_4_eq, _8_to_16_bit_bus_width_converter_1_p4
  or or_1 (or_1_out, comparator_5_eq, comparator_6_eq);
  and and_1 (and_1_out[0], _8_to_16_bit_bus_width_converter_1_p4, or_1_out);
  or or_2 (or_2_out, comparator_5_eq, comparator_7_eq);
  or or_3 (or_3_out, comparator_6_eq, comparator_8_eq);
  ROM #(.AddrBits(16), .Bits(8)) rom_1 (.A(programme_counter_1_p7), .sel(1'b1), .D(alu_1_p1));
  ROM #(.AddrBits(16), .Bits(8)) rom_2 (.A(programme_counter_1_p7), .sel(1'b1), .D(programme_counter_1_p1));
  ROM #(.AddrBits(16), .Bits(16)) rom_3 (.A(programme_counter_1_p7), .sel(1'b1), .D(programme_counter_1_p2));
  RAMDualPort #(.AddrBits(16), .Bits(8)) ramdualport_1 (
    .A(and_1_out), .Din(programme_counter_1_p1), .str(or_2_out), .C(clk), .ld(or_3_out),
    .D(programme_counter_1_p1));
  // Pins of 1 and 16 bits meet at and_1_out

  // Notes on the sheet:
  //   clk: Hz: 10
  //   LN
  //   CMD
  //   DAT
  //   ADR
  //   CLK
  //   LN: output from the programmme counter,
  //   the current line of code being executed
endmodule
